// Logisim project proj_2_1_top.circ as structural Verilog: 7 circuits, main circuit testbench
module TOP (
  input  clk,
  input  rst,
  input  [31:0] inst,
  output [31:0] inst_addr,
  output mem_wen,
  output [31:0] mem_din,
  output [31:0] mem_dout,
  output [31:0] mem_addr,
  output control_en,
  output [31:0] control_pc,
  output wb_en,
  output [4:0] wb_addr,
  output [31:0] wb_data
);

  wire a_nd, add, addi, and_6_out, and_7_out, and_8_out, and_14_out, and_15_out, andi, auipc, B, beq, bge,
       bgeu, blt, bltu, bne, comparator_9_eq, comparator_10_eq, comparator_11_eq, comparator_12_eq,
       comparator_13_eq, comparator_14_eq, comparator_15_eq, comparator_16_eq, comparator_17_eq,
       comparator_18_eq, comparator_19_eq, comparator_20_eq, comparator_21_eq, comparator_22_eq,
       comparator_25_eq, comparator_26_eq, comparator_27_eq, comparator_28_eq, comparator_29_eq,
       comparator_30_eq, comparator_31_eq, comparator_32_eq, comparator_33_eq, comparator_34_eq,
       comparator_35_eq, comparator_36_eq, comparator_37_eq, comparator_38_eq, comparator_39_eq,
       comparator_40_eq, equal, I, I_load, jal, jalr, less, lessu, lh, lui, lw, not_2_out, not_3_out,
       not_4_out, o_r, op2_src, or_1_out, or_2_out, or_3_out, or_4_out, or_5_out, or_6_out, or_7_out,
       or_8_out, or_9_out, or_10_out, or_11_out, or_12_out, or_13_out, or_14_out, or_15_out, or_16_out, ori,
       R, S, s_ll, s_ra, s_rl, sh, slli, slt, slti, sltiu, sltu, srai, srli, sub, sw, U, x_or, xori;
  wire [1:0] op1_src, wb_src;
  wire [3:0] alu_ctrl;
  wire [31:0] alu_result, ctrl_pc, imm, inst_address, mem_out, multiplexer_1_out, multiplexer_5_out,
       multiplexer_6_out, next_inst_addr, PC_add_4, rs1_data, rs2_data, shifter_1_out;

  Priority_Encoder #(.select(2)) priority_encoder_1 (
    .in0(1'b1), .in1(I_load), .in2(or_1_out));  // open: in3, out, gs, en_out, en_in
  or or_1 (or_1_out, jalr, jal);
  or or_2 (or_2_out, slt, slti);
  or or_3 (or_3_out, sltiu, sltu);
  or or_4 (or_4_out, x_or, xori);
  Shifter #(.shift("lr"), .width(32)) shifter_1 (.in(alu_result), .\dist (5'b00001), .out(shifter_1_out));
  Register #(.width(32)) PC (.D(next_inst_addr), .clk(clk), .Q(inst_address), .clr(rst));  // open: en
  Multiplexer #(.select(2), .width(32)) multiplexer_1 (
    .in0(alu_result), .in1(mem_dout), .in2(PC_add_4), .out(multiplexer_1_out), .sel(wb_src));  // open: in3
  or or_5 (or_5_out, s_ll, slli);
  or or_6 (or_6_out, s_rl, srli);
  Comparator #(.mode("unsigned"), .width(5)) comparator_1 (.a(inst[4:0]), .b(5'b10111));  // open: gt, eq, lt
  Comparator #(.mode("unsigned"), .width(7)) comparator_2 (.a(inst[6:0]), .b(7'b0110011));  // open: gt, eq, lt
  Comparator #(.mode("unsigned"), .width(7)) comparator_3 (.a(inst[6:0]), .b(7'b0000011));  // open: gt, eq, lt
  Comparator #(.mode("unsigned"), .width(7)) comparator_4 (.a(inst[6:0]), .b(7'b1100011));  // open: gt, eq, lt
  Comparator #(.mode("unsigned"), .width(7)) comparator_5 (.a(inst[6:0]), .b(7'b1101111));  // open: gt, eq, lt
  Comparator #(.mode("unsigned"), .width(7)) comparator_6 (.a(inst[6:0]), .b(7'b0100011));  // open: gt, eq, lt
  Comparator #(.mode("unsigned"), .width(7)) comparator_7 (.a(inst[6:0]), .b(7'b1100111));  // open: gt, eq, lt
  Comparator #(.mode("unsigned"), .width(7)) comparator_8 (.a(inst[6:0]), .b(7'b0010011));  // open: gt, eq, lt
  Adder #(.width(32)) adder_1 (.a(32'h4), .b(inst_address), .out(PC_add_4));  // open: cin, cout
  Shifter #(.width(32)) shifter_2 (.in(shifter_1_out), .\dist (5'b00001), .out(ctrl_pc));
  or or_7 (or_7_out, ori, o_r);
  or or_8 (or_8_out, s_ra, srai);
  Multiplexer #(.width(32)) multiplexer_2 (.in0(PC_add_4), .in1(ctrl_pc), .out(next_inst_addr), .sel(control_en));
  Multiplexer #(.width(32)) multiplexer_3 (.in0(multiplexer_1_out), .in1({32{1'b0}}), .out(wb_data), .sel(rst));
  or or_9 (or_9_out, andi, a_nd);
  // NOT_Gate not_1 has open pins: in=R, out=open
  Priority_Encoder #(.select(2)) priority_encoder_2 (
    .in0(1'b1), .in1(lui), .in2(or_10_out));  // open: in3, out, gs, en_out, en_in
  or or_10 (or_10_out, auipc, jal, beq);
  Priority_Encoder #(.select(4)) priority_encoder_3 (
    .in0(1'b1), .in1(sub), .in2(or_5_out), .in3(or_2_out), .in4(or_3_out), .in5(or_4_out), .in6(or_6_out),
    .in7(or_8_out), .in8(or_7_out), .in9(or_9_out));  // open: in10, in11, in12, in13, in14, in15, out, gs, en_out, en_in
  Comparator #(.mode("unsigned"), .width(3)) comparator_9 (
    .a(inst[14:12]), .b(3'b000), .eq(comparator_9_eq));  // open: gt, lt
  Comparator #(.mode("unsigned"), .width(7)) comparator_10 (
    .a(inst[31:25]), .b({7{1'b0}}), .eq(comparator_10_eq));  // open: gt, lt
  Comparator #(.mode("unsigned"), .width(3)) comparator_11 (
    .a(inst[14:12]), .b(3'b000), .eq(comparator_11_eq));  // open: gt, lt
  Comparator #(.mode("unsigned"), .width(7)) comparator_12 (
    .a(inst[31:25]), .b(7'b0100000), .eq(comparator_12_eq));  // open: gt, lt
  Comparator #(.mode("unsigned"), .width(3)) comparator_13 (
    .a(inst[14:12]), .b(3'b001), .eq(comparator_13_eq));  // open: gt, lt
  Comparator #(.mode("unsigned"), .width(3)) comparator_14 (
    .a(inst[14:12]), .b(3'b010), .eq(comparator_14_eq));  // open: gt, lt
  Comparator #(.mode("unsigned"), .width(3)) comparator_15 (
    .a(inst[14:12]), .b(3'b110), .eq(comparator_15_eq));  // open: gt, lt
  and and_1 (add, R, comparator_9_eq, comparator_10_eq);
  and and_2 (sub, R, comparator_11_eq, comparator_12_eq);
  and and_3 (s_ll, R, comparator_13_eq);
  and and_4 (slt, R, comparator_14_eq);
  and and_5 (o_r, R, comparator_15_eq);
  Multiplexer multiplexer_4 (.in0(S), .in1(1'b0), .sel(rst));  // open: out
  Multiplexer #(.select(2), .width(32)) multiplexer_5 (
    .in0(rs1_data), .in1({32{1'b0}}), .in2(inst_address), .out(multiplexer_5_out), .sel(op1_src));  // open: in3
  Comparator #(.mode("unsigned"), .width(3)) comparator_16 (
    .a(inst[14:12]), .b(3'b011), .eq(comparator_16_eq));  // open: gt, lt
  Comparator #(.mode("unsigned"), .width(3)) comparator_17 (
    .a(inst[14:12]), .b(3'b100), .eq(comparator_17_eq));  // open: gt, lt
  Comparator #(.mode("unsigned"), .width(3)) comparator_18 (
    .a(inst[14:12]), .b(3'b101), .eq(comparator_18_eq));  // open: gt, lt
  Comparator #(.mode("unsigned"), .width(7)) comparator_19 (
    .a(inst[31:25]), .b({7{1'b0}}), .eq(comparator_19_eq));  // open: gt, lt
  Comparator #(.mode("unsigned"), .width(3)) comparator_20 (
    .a(inst[14:12]), .b(3'b101), .eq(comparator_20_eq));  // open: gt, lt
  Comparator #(.mode("unsigned"), .width(7)) comparator_21 (
    .a(inst[31:25]), .b(7'b0100000), .eq(comparator_21_eq));  // open: gt, lt
  Comparator #(.mode("unsigned"), .width(3)) comparator_22 (
    .a(inst[14:12]), .b(3'b111), .eq(comparator_22_eq));  // open: gt, lt
  Multiplexer #(.width(32)) multiplexer_6 (.in0(rs2_data), .in1(imm), .out(multiplexer_6_out), .sel(op2_src));
  or or_11 (or_11_out, jal, jalr);
  and and_6 (and_6_out, equal, beq);
  not not_2 (not_2_out, equal);
  and and_7 (and_7_out, less, blt);
  and and_8 (and_8_out, lessu, bltu);
  and and_9 (sltu, R, comparator_16_eq);
  and and_10 (x_or, R, comparator_17_eq);
  and and_11 (s_rl, R, comparator_18_eq, comparator_19_eq);
  and and_12 (s_ra, R, comparator_20_eq, comparator_21_eq);
  and and_13 (a_nd, R, comparator_22_eq);
  or or_12 (or_12_out, I, I_load, jalr);
  and and_14 (and_14_out, not_2_out, bne);
  or or_13 (or_13_out, equal, not_3_out);
  not not_3 (not_3_out, less);
  regfile regfile_1 (
    .clk(clk), .rs1(inst[19:15]), .rs2(inst[24:20]), .wb_en(wb_en), .wb_addr(inst[11:7]), .wb_data(wb_data),
    .rs1_data(rs1_data), .rs2_data(rs2_data));
  or or_14 (or_14_out, or_11_out, and_6_out);
  and and_15 (and_15_out, or_13_out, bge);
  // AND_Gate and_16 has open pins: in0=or_15_out, in1=bgeu, out=open
  or or_15 (or_15_out, equal, not_4_out);
  or or_16 (or_16_out, R, or_12_out, U, jal);
  Multiplexer multiplexer_7 (.in0(or_16_out), .in1(1'b0), .sel(rst));  // open: out
  Comparator #(.width(32)) comparator_23 (.a(rs1_data), .b(rs2_data), .lt(less));  // open: gt, eq
  Comparator #(.mode("unsigned"), .width(32)) comparator_24 (
    .a(rs1_data), .b(rs2_data), .eq(equal), .lt(lessu));  // open: gt
  alu alu_1 (.alu_ctrl(alu_ctrl), .rs1(multiplexer_5_out), .rs2(multiplexer_6_out), .alu_result(alu_result));
  Multiplexer multiplexer_8 (.in0(or_14_out), .in1(1'b0), .sel(rst));  // open: out
  not not_4 (not_4_out, lessu);
  Comparator #(.mode("unsigned"), .width(3)) comparator_25 (
    .a(inst[14:12]), .b(3'b000), .eq(comparator_25_eq));  // open: gt, lt
  Comparator #(.mode("unsigned"), .width(3)) comparator_26 (
    .a(inst[14:12]), .b(3'b010), .eq(comparator_26_eq));  // open: gt, lt
  Comparator #(.mode("unsigned"), .width(3)) comparator_27 (
    .a(inst[14:12]), .b(3'b011), .eq(comparator_27_eq));  // open: gt, lt
  Comparator #(.mode("unsigned"), .width(3)) comparator_28 (
    .a(inst[14:12]), .b(3'b100), .eq(comparator_28_eq));  // open: gt, lt
  Comparator #(.mode("unsigned"), .width(3)) comparator_29 (
    .a(inst[14:12]), .b(3'b110), .eq(comparator_29_eq));  // open: gt, lt
  Comparator #(.mode("unsigned"), .width(3)) comparator_30 (
    .a(inst[14:12]), .b(3'b111), .eq(comparator_30_eq));  // open: gt, lt
  Comparator #(.mode("unsigned"), .width(3)) comparator_31 (
    .a(inst[14:12]), .b(3'b001), .eq(comparator_31_eq));  // open: gt, lt
  Multiplexer #(.width(32)) multiplexer_9 (.in0(rs2_data), .in1({32{1'b0}}), .out(mem_din), .sel(rst));
  Multiplexer #(.width(32)) multiplexer_10 (.in0(alu_result), .in1({32{1'b0}}), .out(mem_addr), .sel(rst));
  Multiplexer #(.width(32)) multiplexer_11 (.in0(ctrl_pc), .in1({32{1'b0}}), .out(control_pc), .sel(rst));
  Multiplexer #(.width(5)) multiplexer_12 (.in0(inst[11:7]), .in1({5{1'b0}}), .out(wb_addr), .sel(rst));
  Multiplexer #(.width(32)) multiplexer_13 (.in0(inst_address), .in1({32{1'b0}}), .out(inst_addr), .sel(rst));
  and and_17 (addi, I, comparator_25_eq);
  and and_18 (slti, I, comparator_26_eq);
  and and_19 (sltiu, I, comparator_27_eq);
  and and_20 (xori, I, comparator_28_eq);
  and and_21 (ori, I, comparator_29_eq);
  and and_22 (andi, I, comparator_30_eq);
  and and_23 (slli, I, comparator_31_eq);
  Comparator #(.mode("unsigned"), .width(3)) comparator_32 (
    .a(inst[14:12]), .b(3'b101), .eq(comparator_32_eq));  // open: gt, lt
  Comparator #(.mode("unsigned"), .width(7)) comparator_33 (
    .a(inst[31:25]), .b({7{1'b0}}), .eq(comparator_33_eq));  // open: gt, lt
  Comparator #(.mode("unsigned"), .width(3)) comparator_34 (
    .a(inst[14:12]), .b(3'b101), .eq(comparator_34_eq));  // open: gt, lt
  Comparator #(.mode("unsigned"), .width(7)) comparator_35 (
    .a(inst[31:25]), .b(7'b0100000), .eq(comparator_35_eq));  // open: gt, lt
  Comparator #(.mode("unsigned"), .width(3)) comparator_36 (
    .a(inst[14:12]), .b(3'b010), .eq(comparator_36_eq));  // open: gt, lt
  Comparator #(.mode("unsigned"), .width(3)) comparator_37 (
    .a(inst[14:12]), .b(3'b001), .eq(comparator_37_eq));  // open: gt, lt
  Comparator #(.mode("unsigned"), .width(3)) comparator_38 (
    .a(inst[14:12]), .b(3'b010), .eq(comparator_38_eq));  // open: gt, lt
  Comparator #(.mode("unsigned"), .width(3)) comparator_39 (
    .a(inst[14:12]), .b(3'b001), .eq(comparator_39_eq));  // open: gt, lt
  Multiplexer #(.width(32)) multiplexer_14 (.in0(mem_out), .in1({32{1'b0}}), .out(mem_dout), .sel(rst));
  and and_24 (srli, I, comparator_32_eq, comparator_33_eq);
  and and_25 (srai, I, comparator_34_eq, comparator_35_eq);
  // AND_Gate and_26 has open pins: in0=I_load, in1=comparator_36_eq, out=open
  // AND_Gate and_27 has open pins: in0=I_load, in1=comparator_37_eq, out=open
  // AND_Gate and_28 has open pins: in0=S, in1=comparator_38_eq, out=open
  // AND_Gate and_29 has open pins: in0=S, in1=comparator_39_eq, out=open
  imm_gen imm_gen_1 (.inst(inst), .imm(imm));
  memory memory_1 (
    .lh(lh), .I_load(I_load), .sw(sw), .sh(sh), .rst(rst), .clk(clk), .mem_din(mem_din), .mem_addr(mem_addr),
    .mem_out(mem_out));
  Comparator #(.mode("unsigned"), .width(3)) comparator_40 (
    .a(inst[14:12]), .b(3'b000), .eq(comparator_40_eq));  // open: gt, lt
  Comparator #(.mode("unsigned"), .width(7)) comparator_41 (.a(inst[6:0]), .b(7'b0110111), .eq(lui));  // open: gt, lt
  Comparator #(.mode("unsigned"), .width(7)) comparator_42 (.a(inst[6:0]), .b(7'b0010111), .eq(auipc));  // open: gt, lt
  and and_30 (beq, B, comparator_40_eq);
  controller controller_1 (
    .inst(inst), .rs1_data(rs1_data), .rs2_data(rs2_data), .alu_ctrl(alu_ctrl), .control_en(control_en),
    .wb_src(wb_src), .op1_src(op1_src), .op2_src(op2_src), .mem_wen(mem_wen), .wb_en(wb_en), .U(U), .R(R),
    .I_load(I_load), .B(B), .jal(jal), .S(S), .jalr(jalr), .I(I), .lw(lw), .lh(lh), .sw(sw), .sh(sh));  // open: flush

  // Other names for the same wires on the sheet: opcode[6:0] = inst[6:0]; imm_4_0[4:0] = inst[11:7];
  //   imm_11_b = inst[7]; wb_address[4:0] = inst[11:7]; imm_4_1[3:0] = inst[11:8]; func3[2:0] = inst[14:12];
  //   imm_19_12[7:0] = inst[19:12]; imm_31_12[19:0] = inst[31:12]; rs1[4:0] = inst[19:15];
  //   imm_11_0[11:0] = inst[31:20]; imm_11_j = inst[20]; rs2[4:0] = inst[24:20]; imm_10_1[9:0] = inst[30:21];
  //   func7[6:0] = inst[31:25]; imm_10_5[5:0] = inst[30:25]; imm_11_5[6:0] = inst[31:25]; imm_12 = inst[31];
  //   imm_20 = inst[31]

  // Notes on the sheet:
  //   PC
  //   WB
  //   wb_src
  //   alu_ctrl
  //   DON'T TOUCH!
  //   op1_src, op2_src
  //   Decode
  //   mem_wen
  //   Exec
  //   control_en
  //   rs1, rs2, compare
  //   Mem
  //   imm Gen
endmodule

module testbench (
  input  rst,
  output [5:0] out_2,
  output out_3,
  output halt,
  output [31:0] out_5,
  output [31:0] mem_dout,
  output [31:0] mem_addr,
  output out_8,
  output [31:0] out_9,
  output out_10,
  output [4:0] out_11,
  output [31:0] out_12
);

  wire and_1_out, carry, clk, not_1_out, not_2_out, por_1_out, rst_t;
  wire [31:0] inst, inst_addr;

  not not_1 (not_1_out, inst[2]);
  not not_2 (not_2_out, inst[3]);
  POR por_1 (.out(por_1_out));
  TOP top_1 (
    .clk(clk), .rst(rst_t), .inst(inst), .inst_addr(inst_addr), .mem_wen(out_3), .mem_din(out_5),
    .mem_dout(mem_dout), .mem_addr(mem_addr), .control_en(out_8), .control_pc(out_9), .wb_en(out_10),
    .wb_addr(out_11), .wb_data(out_12));
  Clock clock_1 (.out(clk));
  or or_1 (rst_t, rst, por_1_out);
  and and_1 (and_1_out, inst[0], inst[1], not_1_out, not_2_out, inst[4], inst[5], inst[6]);
  or or_2 (halt, and_1_out, carry);
  Counter #(.max('h3f), .width(6)) counter_1 (
    .clr(rst_t), .up(1'b1), .count(1'b1), .clk(clk), .carry(carry), .Q(out_2));  // open: load, D
  // ROM #(.line("quad"), .misaligned("true")) inst_mem: pin names not known; wires that end beside it: inst_addr[7:0], inst[7:0], inst[15:8], inst[23:16], inst[31:24]
  // Probe on inst

  // Other names for the same wires on the sheet: control_en = out_8; control_pc[31:0] = out_9; mem_din[31:0] = out_5;
  //   mem_wen = out_3; wb_addr[4:0] = out_11; wb_data[31:0] = out_12; wb_en = out_10

  // Notes on the sheet:
  //   DON'T TOUCH!
  //   contents of inst_mem (hex, n*v repeats v):
  //   37 f1 33 26 23 90 20 0 ef f0 df ff b3 80 30
  //   you can write any instruction in
endmodule

module regfile (
  input  clk,
  input  [4:0] rs1,
  input  [4:0] rs2,
  input  wb_en,
  input  [4:0] wb_addr,
  input  [31:0] wb_data,
  output [31:0] rs1_data,
  output [31:0] rs2_data
);

  wire rst;
  wire [3:0] demultiplexer_1_out0, demultiplexer_1_out4, demultiplexer_1_out8, demultiplexer_1_out12,
       demultiplexer_1_out16, demultiplexer_1_out20, demultiplexer_1_out24, demultiplexer_1_out28;
  wire [31:0] x0_q, x1_q, x2_q, x3_q, x4_q, x5_q, x6_q, x7_q, x8_q, x9_q, x10_q, x11_q, x12_q, x13_q, x14_q,
       x15_q, x16_q, x17_q, x18_q, x19_q, x20_q, x21_q, x22_q, x23_q, x24_q, x25_q, x26_q, x27_q, x28_q,
       x29_q, x30_q, x31_q;

  Demultiplexer #(.select(5)) demultiplexer_1 (
    .out0(demultiplexer_1_out0[0]), .out1(demultiplexer_1_out0[1]), .out2(demultiplexer_1_out0[2]),
    .out3(demultiplexer_1_out0[3]), .out4(demultiplexer_1_out4[0]), .out5(demultiplexer_1_out4[1]),
    .out6(demultiplexer_1_out4[2]), .out7(demultiplexer_1_out4[3]), .out8(demultiplexer_1_out8[0]),
    .out9(demultiplexer_1_out8[1]), .out10(demultiplexer_1_out8[2]), .out11(demultiplexer_1_out8[3]),
    .out12(demultiplexer_1_out12[0]), .out13(demultiplexer_1_out12[1]), .out14(demultiplexer_1_out12[2]),
    .out15(demultiplexer_1_out12[3]), .out16(demultiplexer_1_out16[0]), .out17(demultiplexer_1_out16[1]),
    .out18(demultiplexer_1_out16[2]), .out19(demultiplexer_1_out16[3]), .out20(demultiplexer_1_out20[0]),
    .out21(demultiplexer_1_out20[1]), .out22(demultiplexer_1_out20[2]), .out23(demultiplexer_1_out20[3]),
    .out24(demultiplexer_1_out24[0]), .out25(demultiplexer_1_out24[1]), .out26(demultiplexer_1_out24[2]),
    .out27(demultiplexer_1_out24[3]), .out28(demultiplexer_1_out28[0]), .out29(demultiplexer_1_out28[1]),
    .out30(demultiplexer_1_out28[2]), .out31(demultiplexer_1_out28[3]), .in(wb_en), .sel(wb_addr));
  Register #(.width(32)) x0 (.D(wb_data), .en(1'b0), .clk(clk), .Q(x0_q), .clr(rst));
  Register #(.width(32)) x4 (.D(wb_data), .en(demultiplexer_1_out4[0]), .clk(clk), .Q(x4_q), .clr(rst));
  Register #(.width(32)) x8 (.D(wb_data), .en(demultiplexer_1_out8[0]), .clk(clk), .Q(x8_q), .clr(rst));
  Register #(.width(32)) x12 (.D(wb_data), .en(demultiplexer_1_out12[0]), .clk(clk), .Q(x12_q), .clr(rst));
  Register #(.width(32)) x16 (.D(wb_data), .en(demultiplexer_1_out16[0]), .clk(clk), .Q(x16_q), .clr(rst));
  Register #(.width(32)) x20 (.D(wb_data), .en(demultiplexer_1_out20[0]), .clk(clk), .Q(x20_q), .clr(rst));
  Register #(.width(32)) x24 (.D(wb_data), .en(demultiplexer_1_out24[0]), .clk(clk), .Q(x24_q), .clr(rst));
  Register #(.width(32)) x28 (.D(wb_data), .en(demultiplexer_1_out28[0]), .clk(clk), .Q(x28_q), .clr(rst));
  Register #(.width(32)) x1 (.D(wb_data), .en(demultiplexer_1_out0[1]), .clk(clk), .Q(x1_q), .clr(rst));
  Register #(.width(32)) x5 (.D(wb_data), .en(demultiplexer_1_out4[1]), .clk(clk), .Q(x5_q), .clr(rst));
  Register #(.width(32)) x9 (.D(wb_data), .en(demultiplexer_1_out8[1]), .clk(clk), .Q(x9_q), .clr(rst));
  Register #(.width(32)) x13 (.D(wb_data), .en(demultiplexer_1_out12[1]), .clk(clk), .Q(x13_q), .clr(rst));
  Register #(.width(32)) x17 (.D(wb_data), .en(demultiplexer_1_out16[1]), .clk(clk), .Q(x17_q), .clr(rst));
  Register #(.width(32)) x21 (.D(wb_data), .en(demultiplexer_1_out20[1]), .clk(clk), .Q(x21_q), .clr(rst));
  Register #(.width(32)) x25 (.D(wb_data), .en(demultiplexer_1_out24[1]), .clk(clk), .Q(x25_q), .clr(rst));
  Register #(.width(32)) x29 (.D(wb_data), .en(demultiplexer_1_out28[1]), .clk(clk), .Q(x29_q), .clr(rst));
  Register #(.width(32)) x2 (.D(wb_data), .en(demultiplexer_1_out0[2]), .clk(clk), .Q(x2_q), .clr(rst));
  Register #(.width(32)) x6 (.D(wb_data), .en(demultiplexer_1_out4[2]), .clk(clk), .Q(x6_q), .clr(rst));
  Register #(.width(32)) x10 (.D(wb_data), .en(demultiplexer_1_out8[2]), .clk(clk), .Q(x10_q), .clr(rst));
  Register #(.width(32)) x14 (.D(wb_data), .en(demultiplexer_1_out12[2]), .clk(clk), .Q(x14_q), .clr(rst));
  Register #(.width(32)) x18 (.D(wb_data), .en(demultiplexer_1_out16[2]), .clk(clk), .Q(x18_q), .clr(rst));
  Register #(.width(32)) x22 (.D(wb_data), .en(demultiplexer_1_out20[2]), .clk(clk), .Q(x22_q), .clr(rst));
  Register #(.width(32)) x26 (.D(wb_data), .en(demultiplexer_1_out24[2]), .clk(clk), .Q(x26_q), .clr(rst));
  Register #(.width(32)) x30 (.D(wb_data), .en(demultiplexer_1_out28[2]), .clk(clk), .Q(x30_q), .clr(rst));
  Register #(.width(32)) x3 (.D(wb_data), .en(demultiplexer_1_out0[3]), .clk(clk), .Q(x3_q), .clr(rst));
  Register #(.width(32)) x7 (.D(wb_data), .en(demultiplexer_1_out4[3]), .clk(clk), .Q(x7_q), .clr(rst));
  Register #(.width(32)) x11 (.D(wb_data), .en(demultiplexer_1_out8[3]), .clk(clk), .Q(x11_q), .clr(rst));
  Register #(.width(32)) x15 (.D(wb_data), .en(demultiplexer_1_out12[3]), .clk(clk), .Q(x15_q), .clr(rst));
  Register #(.width(32)) x19 (.D(wb_data), .en(demultiplexer_1_out16[3]), .clk(clk), .Q(x19_q), .clr(rst));
  Register #(.width(32)) x23 (.D(wb_data), .en(demultiplexer_1_out20[3]), .clk(clk), .Q(x23_q), .clr(rst));
  Register #(.width(32)) x27 (.D(wb_data), .en(demultiplexer_1_out24[3]), .clk(clk), .Q(x27_q), .clr(rst));
  Register #(.width(32)) x31 (.D(wb_data), .en(demultiplexer_1_out28[3]), .clk(clk), .Q(x31_q), .clr(rst));
  Multiplexer #(.select(5), .width(32)) multiplexer_1 (
    .in0(x0_q), .in1(x1_q), .in2(x2_q), .in3(x3_q), .in4(x4_q), .in5(x5_q), .in6(x6_q), .in7(x7_q),
    .in8(x8_q), .in9(x9_q), .in10(x10_q), .in11(x11_q), .in12(x12_q), .in13(x13_q), .in14(x14_q),
    .in15(x15_q), .in16(x16_q), .in17(x17_q), .in18(x18_q), .in19(x19_q), .in20(x20_q), .in21(x21_q),
    .in22(x22_q), .in23(x23_q), .in24(x24_q), .in25(x25_q), .in26(x26_q), .in27(x27_q), .in28(x28_q),
    .in29(x29_q), .in30(x30_q), .in31(x31_q), .out(rs1_data), .sel(rs1));
  Multiplexer #(.select(5), .width(32)) multiplexer_2 (
    .in0(x0_q), .in1(x1_q), .in2(x2_q), .in3(x3_q), .in4(x4_q), .in5(x5_q), .in6(x6_q), .in7(x7_q),
    .in8(x8_q), .in9(x9_q), .in10(x10_q), .in11(x11_q), .in12(x12_q), .in13(x13_q), .in14(x14_q),
    .in15(x15_q), .in16(x16_q), .in17(x17_q), .in18(x18_q), .in19(x19_q), .in20(x20_q), .in21(x21_q),
    .in22(x22_q), .in23(x23_q), .in24(x24_q), .in25(x25_q), .in26(x26_q), .in27(x27_q), .in28(x28_q),
    .in29(x29_q), .in30(x30_q), .in31(x31_q), .out(rs2_data), .sel(rs2));
endmodule

module imm_gen (
  input  [31:0] inst,
  output [31:0] imm
);

  wire B, I, I_load, jal, jalr, or_1_out, R, S, U;
  wire [2:0] imm_sel;
  wire [31:0] bit_extender_1_out, bit_extender_2_out, bit_extender_3_out, bit_extender_4_out;

  Comparator #(.mode("unsigned"), .width(5)) comparator_1 (.a(inst[4:0]), .b(5'b10111), .eq(U));  // open: gt, lt
  Comparator #(.mode("unsigned"), .width(7)) comparator_2 (.a(inst[6:0]), .b(7'b0110011), .eq(R));  // open: gt, lt
  Comparator #(.mode("unsigned"), .width(7)) comparator_3 (.a(inst[6:0]), .b(7'b0000011), .eq(I_load));  // open: gt, lt
  Comparator #(.mode("unsigned"), .width(7)) comparator_4 (.a(inst[6:0]), .b(7'b1100011), .eq(B));  // open: gt, lt
  Comparator #(.mode("unsigned"), .width(7)) comparator_5 (.a(inst[6:0]), .b(7'b1101111), .eq(jal));  // open: gt, lt
  Comparator #(.mode("unsigned"), .width(7)) comparator_6 (.a(inst[6:0]), .b(7'b0100011), .eq(S));  // open: gt, lt
  Comparator #(.mode("unsigned"), .width(7)) comparator_7 (.a(inst[6:0]), .b(7'b1100111), .eq(jalr));  // open: gt, lt
  Comparator #(.mode("unsigned"), .width(7)) comparator_8 (.a(inst[6:0]), .b(7'b0010011), .eq(I));  // open: gt, lt
  or or_1 (or_1_out, I_load, I, jalr);
  assign bit_extender_1_out = {{20{inst[31]}}, {inst[31:25], inst[11:7]}};  // Bit_Extender bit_extender_1
  assign bit_extender_2_out = {{20{inst[31]}}, inst[31:20]};  // Bit_Extender bit_extender_2
  Priority_Encoder priority_encoder_1 (
    .in0(U), .in1(jal), .in2(B), .in3(S), .in4(or_1_out), .out(imm_sel));  // open: in5, in6, in7, en_in, gs, en_out
  assign bit_extender_3_out = {{11{inst[31]}}, {inst[31], inst[19:12], inst[20], inst[30:21], 1'b0}};  // Bit_Extender bit_extender_3
  assign bit_extender_4_out = {{19{inst[31]}}, {inst[31], inst[7], inst[30:25], inst[11:8], 1'b0}};  // Bit_Extender bit_extender_4
  Multiplexer #(.select(3), .width(32)) multiplexer_1 (
    .in0({inst[31:12], {12{1'b0}}}), .in1(bit_extender_3_out), .in2(bit_extender_4_out),
    .in3(bit_extender_1_out), .in4(bit_extender_2_out), .out(imm), .sel(imm_sel));  // open: in5, in6, in7

  // Other names for the same wires on the sheet: imm_4_0[4:0] = inst[11:7]; imm_4_1[3:0] = inst[11:8];
  //   wb_addr[4:0] = inst[11:7]; imm_11_b = inst[7]; func3[2:0] = inst[14:12]; imm_19_12[7:0] = inst[19:12];
  //   imm_31_12[19:0] = inst[31:12]; rs1[4:0] = inst[19:15]; imm_11_0[11:0] = inst[31:20]; imm_11_j = inst[20];
  //   rs2[4:0] = inst[24:20]; imm_10_1[9:0] = inst[30:21]; func7[6:0] = inst[31:25]; imm_10_5[5:0] = inst[30:25];
  //   imm_11_5[6:0] = inst[31:25]; imm_12 = inst[31]; imm_20 = inst[31]; opcode[6:0] = inst[6:0]
endmodule

module alu (
  input  [3:0] alu_ctrl,
  input  [31:0] rs1,
  input  [31:0] rs2,
  output [31:0] alu_result
);

  wire [0:0] comparator_1_lt, comparator_2_lt;
  wire [31:0] adder_1_out, and_1_out, or_1_out, shifter_1_out, shifter_2_out, shifter_3_out,
       subtractor_1_out, xor_1_out;

  Adder #(.width(32)) adder_1 (.a(rs1), .b(rs2), .out(adder_1_out));  // open: cin, cout
  Subtractor #(.width(32)) subtractor_1 (.a(rs1), .b(rs2), .out(subtractor_1_out));  // open: bin, bout
  Shifter #(.width(32)) shifter_1 (.in(rs1), .\dist (rs2[4:0]), .out(shifter_1_out));
  Comparator #(.width(32)) comparator_1 (.a(rs1), .b(rs2), .lt(comparator_1_lt[0]));  // open: gt, eq
  Comparator #(.mode("unsigned"), .width(32)) comparator_2 (.a(rs1), .b(rs2), .lt(comparator_2_lt[0]));  // open: gt, eq
  assign xor_1_out = rs1 ^ rs2;  // XOR_Gate xor_1, 32 bits wide
  Shifter #(.shift("lr"), .width(32)) shifter_2 (.in(rs1), .\dist (rs2[4:0]), .out(shifter_2_out));
  Shifter #(.shift("ar"), .width(32)) shifter_3 (.in(rs1), .\dist (rs2[4:0]), .out(shifter_3_out));
  assign or_1_out = rs1 | rs2;  // OR_Gate or_1, 32 bits wide
  assign and_1_out = rs1 & rs2;  // AND_Gate and_1, 32 bits wide
  Multiplexer #(.select(4), .width(32)) multiplexer_1 (
    .in0(adder_1_out), .in1(subtractor_1_out), .in2(shifter_1_out), .in3({{31{1'b0}}, comparator_1_lt[0]}),
    .in4({{31{1'b0}}, comparator_2_lt[0]}), .in5(xor_1_out), .in6(shifter_2_out), .in7(shifter_3_out),
    .in8(or_1_out), .in9(and_1_out), .out(alu_result), .sel(alu_ctrl));  // open: in10, in11, in12, in13, in14, in15
endmodule

module memory (
  input  lh,
  input  I_load,
  input  sw,
  input  sh,
  input  rst,
  input  clk,
  input  [31:0] mem_din,
  input  [31:0] mem_addr,
  output [31:0] mem_out
);

  wire align, and_1_out, and_2_out, and_3_out, and_4_out, mem_1, mem_2, mem_3, mem_4, one, or_1_out,
       or_2_out, or_5_out, or_6_out, three, two;
  wire [7:0] Byte_1, Byte_2, Byte_3, Byte_4;
  wire [15:0] adder_1_out, adder_2_out, adder_3_out, mem, mem_B1, mem_B2, mem_B3, mem_B4, shifter_1_out;
  wire [31:0] bit_extender_1_out, mem_din_final, multiplexer_1_out;

  RAM #(.addrWidth(16), .asyncread("true"), .clearpin("true")) ram_1 (
    .addr(mem_B1), .we(mem_1), .oe(I_load), .clk(clk), .din(mem_din_final[7:0]), .dout(Byte_1), .clr(rst));
  RAM #(.addrWidth(16), .asyncread("true"), .clearpin("true")) ram_2 (
    .addr(mem_B2), .we(mem_2), .oe(I_load), .clk(clk), .din(mem_din_final[15:8]), .dout(Byte_2), .clr(rst));
  Shifter #(.shift("lr"), .width(16)) shifter_1 (.in(mem_addr[15:0]), .\dist (4'b0010), .out(shifter_1_out));
  Shifter #(.width(16)) shifter_2 (.in(shifter_1_out), .\dist (4'b0010), .out(mem));
  or or_1 (or_1_out, align, three);
  or or_2 (or_2_out, align, one);
  or or_3 (mem_1, sw, and_1_out);
  and and_1 (and_1_out, sh, or_1_out);
  or or_4 (mem_2, sw, and_2_out);
  and and_2 (and_2_out, sh, or_2_out);
  RAM #(.addrWidth(16), .asyncread("true"), .clearpin("true")) ram_3 (
    .addr(mem_B3), .we(mem_3), .oe(I_load), .clk(clk), .din(mem_din_final[23:16]), .dout(Byte_3), .clr(rst));
  RAM #(.addrWidth(16), .asyncread("true"), .clearpin("true")) ram_4 (
    .addr(mem_B4), .we(mem_4), .oe(I_load), .clk(clk), .din(mem_din_final[31:24]), .dout(Byte_4), .clr(rst));
  and and_3 (and_3_out, sh, or_5_out);
  or or_5 (or_5_out, one, two);
  and and_4 (and_4_out, sh, or_6_out);
  or or_6 (or_6_out, two, three);
  or or_7 (mem_3, sw, and_3_out);
  or or_8 (mem_4, sw, and_4_out);
  Adder #(.width(16)) adder_1 (.a(mem), .b(16'h4), .out(adder_1_out));  // open: cin, cout
  Adder #(.width(16)) adder_2 (.a(mem), .b(16'h4), .out(adder_2_out));  // open: cin, cout
  Adder #(.width(16)) adder_3 (.a(mem), .b(16'h4), .out(adder_3_out));  // open: cin, cout
  Adder #(.width(16)) adder_4 (.a(mem), .b(16'h4));  // open: out, cin, cout
  Multiplexer #(.select(2), .width(32)) multiplexer_1 (
    .in0({Byte_4, Byte_3, Byte_2, Byte_1}), .in1({Byte_1, Byte_4, Byte_3, Byte_2}),
    .in2({Byte_2, Byte_1, Byte_4, Byte_3}), .in3({Byte_3, Byte_2, Byte_1, Byte_4}), .out(multiplexer_1_out),
    .sel(mem_addr[1:0]));
  Multiplexer #(.select(2), .width(16)) multiplexer_2 (
    .in0(mem), .in1(adder_1_out), .in2(adder_1_out), .in3(adder_1_out), .out(mem_B1), .sel(mem_addr[1:0]));
  Multiplexer #(.select(2), .width(16)) multiplexer_3 (
    .in0(mem), .in1(mem), .in2(adder_2_out), .in3(adder_2_out), .out(mem_B2), .sel(mem_addr[1:0]));
  Multiplexer #(.select(2), .width(16)) multiplexer_4 (
    .in0(mem), .in1(mem), .in2(mem), .in3(adder_3_out), .out(mem_B3), .sel(mem_addr[1:0]));
  Multiplexer #(.select(2), .width(16)) multiplexer_5 (
    .in0(mem), .in1(mem), .in2(mem), .in3(mem), .out(mem_B4), .sel(mem_addr[1:0]));
  Multiplexer #(.width(32)) multiplexer_6 (.in0(multiplexer_1_out), .in1(bit_extender_1_out), .out(mem_out), .sel(lh));
  assign bit_extender_1_out = {{16{multiplexer_1_out[15]}}, multiplexer_1_out[15:0]};  // Bit_Extender bit_extender_1
  Multiplexer #(.select(2), .width(32)) multiplexer_7 (
    .in0(mem_din), .in1({mem_din[23:0], mem_din[31:24]}), .in2({mem_din[15:0], mem_din[31:16]}),
    .in3({mem_din[7:0], mem_din[31:8]}), .out(mem_din_final), .sel(mem_addr[1:0]));
  Comparator #(.mode("unsigned"), .width(2)) comparator_1 (
    .a(mem_addr[1:0]), .b(2'b01), .eq(one), .lt(align));  // open: gt
  Comparator #(.mode("unsigned"), .width(2)) comparator_2 (.a(mem_addr[1:0]), .b(2'b11), .eq(three));  // open: gt, lt
  Comparator #(.mode("unsigned"), .width(2)) comparator_3 (.a(mem_addr[1:0]), .b(2'b10), .eq(two));  // open: gt, lt

  // Other names for the same wires on the sheet: mem_sel[1:0] = mem_addr[1:0]; mem_din_1[31:0] = mem_din;
  //   mem_din_2[31:0] = {mem_din[23:0], mem_din[31:24]}; mem_din_3[31:0] = {mem_din[15:0], mem_din[31:16]};
  //   mem_din_4[31:0] = {mem_din[7:0], mem_din[31:8]}; mem_din_B4[7:0] = mem_din[31:24];
  //   mem_din_B1[7:0] = mem_din[7:0]; mem_din_B2[7:0] = mem_din[15:8]; mem_din_B3[7:0] = mem_din[23:16];
  //   out_1[31:0] = {Byte_4, Byte_3, Byte_2, Byte_1}; out_2[31:0] = {Byte_1, Byte_4, Byte_3, Byte_2};
  //   out_3[31:0] = {Byte_2, Byte_1, Byte_4, Byte_3}; out_4[31:0] = {Byte_3, Byte_2, Byte_1, Byte_4}
endmodule

module controller (
  input  [31:0] inst,
  input  [31:0] rs1_data,
  input  [31:0] rs2_data,
  output [3:0] alu_ctrl,
  output control_en,
  output [1:0] wb_src,
  output [1:0] op1_src,
  output op2_src,
  output mem_wen,
  output wb_en,
  output flush,
  output U,
  output R,
  output I_load,
  output B,
  output jal,
  output S,
  output jalr,
  output I,
  output lw,
  output lh,
  output sw,
  output sh
);

  wire a_nd, add, addi, and_6_out, andi, auipc, beq, comparator_9_eq, comparator_10_eq, comparator_11_eq,
       comparator_12_eq, comparator_13_eq, comparator_14_eq, comparator_15_eq, comparator_16_eq,
       comparator_17_eq, comparator_18_eq, comparator_19_eq, comparator_20_eq, comparator_21_eq,
       comparator_22_eq, comparator_23_eq, comparator_24_eq, comparator_25_eq, comparator_26_eq,
       comparator_27_eq, comparator_28_eq, comparator_29_eq, comparator_30_eq, comparator_31_eq,
       comparator_32_eq, comparator_33_eq, comparator_34_eq, comparator_35_eq, comparator_36_eq,
       comparator_37_eq, comparator_38_eq, equal, lui, o_r, or_1_out, or_2_out, or_3_out, or_4_out, or_5_out,
       or_6_out, or_7_out, or_8_out, or_9_out, or_11_out, or_12_out, or_13_out, ori, s_ll, s_ra, s_rl, slli,
       slt, slti, sltiu, sltu, srai, srli, sub, x_or, xori;

  or or_1 (or_1_out, slt, slti);
  or or_2 (or_2_out, sltiu, sltu);
  or or_3 (or_3_out, x_or, xori);
  or or_4 (or_4_out, s_ll, slli);
  or or_5 (or_5_out, s_rl, srli);
  Comparator #(.mode("unsigned"), .width(5)) comparator_1 (.a(inst[4:0]), .b(5'b10111), .eq(U));  // open: gt, lt
  Comparator #(.mode("unsigned"), .width(7)) comparator_2 (.a(inst[6:0]), .b(7'b0110011), .eq(R));  // open: gt, lt
  Comparator #(.mode("unsigned"), .width(7)) comparator_3 (.a(inst[6:0]), .b(7'b0000011), .eq(I_load));  // open: gt, lt
  Comparator #(.mode("unsigned"), .width(7)) comparator_4 (.a(inst[6:0]), .b(7'b1100011), .eq(B));  // open: gt, lt
  Comparator #(.mode("unsigned"), .width(7)) comparator_5 (.a(inst[6:0]), .b(7'b1101111), .eq(jal));  // open: gt, lt
  Comparator #(.mode("unsigned"), .width(7)) comparator_6 (
    .a(inst[6:0]), .b(7'b0100011), .eq(mem_wen));  // open: gt, lt
  Comparator #(.mode("unsigned"), .width(7)) comparator_7 (.a(inst[6:0]), .b(7'b1100111), .eq(jalr));  // open: gt, lt
  Comparator #(.mode("unsigned"), .width(7)) comparator_8 (.a(inst[6:0]), .b(7'b0010011), .eq(I));  // open: gt, lt
  or or_6 (or_6_out, ori, o_r);
  or or_7 (or_7_out, s_ra, srai);
  or or_8 (or_8_out, andi, a_nd);
  Priority_Encoder #(.select(4)) priority_encoder_1 (
    .in0(1'b1), .in1(sub), .in2(or_4_out), .in3(or_1_out), .in4(or_2_out), .in5(or_3_out), .in6(or_5_out),
    .in7(or_7_out), .in8(or_6_out), .in9(or_8_out), .out(alu_ctrl));  // open: in10, in11, in12, in13, in14, in15, gs, en_out, en_in
  Comparator #(.mode("unsigned"), .width(3)) comparator_9 (
    .a(inst[14:12]), .b(3'b000), .eq(comparator_9_eq));  // open: gt, lt
  Comparator #(.mode("unsigned"), .width(7)) comparator_10 (
    .a(inst[31:25]), .b({7{1'b0}}), .eq(comparator_10_eq));  // open: gt, lt
  Comparator #(.mode("unsigned"), .width(3)) comparator_11 (
    .a(inst[14:12]), .b(3'b000), .eq(comparator_11_eq));  // open: gt, lt
  Comparator #(.mode("unsigned"), .width(7)) comparator_12 (
    .a(inst[31:25]), .b(7'b0100000), .eq(comparator_12_eq));  // open: gt, lt
  Comparator #(.mode("unsigned"), .width(3)) comparator_13 (
    .a(inst[14:12]), .b(3'b001), .eq(comparator_13_eq));  // open: gt, lt
  Comparator #(.mode("unsigned"), .width(3)) comparator_14 (
    .a(inst[14:12]), .b(3'b010), .eq(comparator_14_eq));  // open: gt, lt
  Comparator #(.mode("unsigned"), .width(3)) comparator_15 (
    .a(inst[14:12]), .b(3'b110), .eq(comparator_15_eq));  // open: gt, lt
  and and_1 (add, R, comparator_9_eq, comparator_10_eq);
  and and_2 (sub, R, comparator_11_eq, comparator_12_eq);
  and and_3 (s_ll, R, comparator_13_eq);
  and and_4 (slt, R, comparator_14_eq);
  and and_5 (o_r, R, comparator_15_eq);
  or or_9 (or_9_out, jal, jalr);
  and and_6 (and_6_out, equal, beq);
  Comparator #(.mode("unsigned"), .width(3)) comparator_16 (
    .a(inst[14:12]), .b(3'b011), .eq(comparator_16_eq));  // open: gt, lt
  Comparator #(.mode("unsigned"), .width(3)) comparator_17 (
    .a(inst[14:12]), .b(3'b100), .eq(comparator_17_eq));  // open: gt, lt
  Comparator #(.mode("unsigned"), .width(3)) comparator_18 (
    .a(inst[14:12]), .b(3'b101), .eq(comparator_18_eq));  // open: gt, lt
  Comparator #(.mode("unsigned"), .width(7)) comparator_19 (
    .a(inst[31:25]), .b({7{1'b0}}), .eq(comparator_19_eq));  // open: gt, lt
  Comparator #(.mode("unsigned"), .width(3)) comparator_20 (
    .a(inst[14:12]), .b(3'b101), .eq(comparator_20_eq));  // open: gt, lt
  Comparator #(.mode("unsigned"), .width(7)) comparator_21 (
    .a(inst[31:25]), .b(7'b0100000), .eq(comparator_21_eq));  // open: gt, lt
  Comparator #(.mode("unsigned"), .width(3)) comparator_22 (
    .a(inst[14:12]), .b(3'b111), .eq(comparator_22_eq));  // open: gt, lt
  or or_10 (control_en, or_9_out, and_6_out);
  and and_7 (sltu, R, comparator_16_eq);
  and and_8 (x_or, R, comparator_17_eq);
  and and_9 (s_rl, R, comparator_18_eq, comparator_19_eq);
  and and_10 (s_ra, R, comparator_20_eq, comparator_21_eq);
  and and_11 (a_nd, R, comparator_22_eq);
  Comparator #(.mode("unsigned"), .width(3)) comparator_23 (
    .a(inst[14:12]), .b(3'b000), .eq(comparator_23_eq));  // open: gt, lt
  Comparator #(.mode("unsigned"), .width(3)) comparator_24 (
    .a(inst[14:12]), .b(3'b010), .eq(comparator_24_eq));  // open: gt, lt
  Comparator #(.mode("unsigned"), .width(3)) comparator_25 (
    .a(inst[14:12]), .b(3'b011), .eq(comparator_25_eq));  // open: gt, lt
  Comparator #(.mode("unsigned"), .width(3)) comparator_26 (
    .a(inst[14:12]), .b(3'b100), .eq(comparator_26_eq));  // open: gt, lt
  Comparator #(.mode("unsigned"), .width(3)) comparator_27 (
    .a(inst[14:12]), .b(3'b110), .eq(comparator_27_eq));  // open: gt, lt
  Comparator #(.mode("unsigned"), .width(3)) comparator_28 (
    .a(inst[14:12]), .b(3'b111), .eq(comparator_28_eq));  // open: gt, lt
  Comparator #(.mode("unsigned"), .width(3)) comparator_29 (
    .a(inst[14:12]), .b(3'b001), .eq(comparator_29_eq));  // open: gt, lt
  and and_12 (addi, I, comparator_23_eq);
  and and_13 (slti, I, comparator_24_eq);
  and and_14 (sltiu, I, comparator_25_eq);
  and and_15 (xori, I, comparator_26_eq);
  and and_16 (ori, I, comparator_27_eq);
  and and_17 (andi, I, comparator_28_eq);
  and and_18 (slli, I, comparator_29_eq);
  Priority_Encoder #(.select(2)) priority_encoder_2 (
    .in0(1'b1), .in1(I_load), .in2(or_11_out), .out(wb_src));  // open: in3, gs, en_out, en_in
  or or_11 (or_11_out, jalr, jal);
  Comparator #(.mode("unsigned"), .width(3)) comparator_30 (
    .a(inst[14:12]), .b(3'b101), .eq(comparator_30_eq));  // open: gt, lt
  Comparator #(.mode("unsigned"), .width(7)) comparator_31 (
    .a(inst[31:25]), .b({7{1'b0}}), .eq(comparator_31_eq));  // open: gt, lt
  Comparator #(.mode("unsigned"), .width(3)) comparator_32 (
    .a(inst[14:12]), .b(3'b101), .eq(comparator_32_eq));  // open: gt, lt
  Comparator #(.mode("unsigned"), .width(7)) comparator_33 (
    .a(inst[31:25]), .b(7'b0100000), .eq(comparator_33_eq));  // open: gt, lt
  Comparator #(.mode("unsigned"), .width(3)) comparator_34 (
    .a(inst[14:12]), .b(3'b010), .eq(comparator_34_eq));  // open: gt, lt
  Comparator #(.mode("unsigned"), .width(3)) comparator_35 (
    .a(inst[14:12]), .b(3'b001), .eq(comparator_35_eq));  // open: gt, lt
  Comparator #(.mode("unsigned"), .width(3)) comparator_36 (
    .a(inst[14:12]), .b(3'b010), .eq(comparator_36_eq));  // open: gt, lt
  Comparator #(.mode("unsigned"), .width(3)) comparator_37 (
    .a(inst[14:12]), .b(3'b001), .eq(comparator_37_eq));  // open: gt, lt
  and and_19 (srli, I, comparator_30_eq, comparator_31_eq);
  and and_20 (srai, I, comparator_32_eq, comparator_33_eq);
  and and_21 (lw, I_load, comparator_34_eq);
  and and_22 (lh, I_load, comparator_35_eq);
  and and_23 (sw, mem_wen, comparator_36_eq);
  and and_24 (sh, mem_wen, comparator_37_eq);
  not not_1 (op2_src, R);
  or or_12 (or_12_out, auipc, jal, beq);
  Priority_Encoder #(.select(2)) priority_encoder_3 (
    .in0(1'b1), .in1(lui), .in2(or_12_out), .out(op1_src));  // open: in3, gs, en_out, en_in
  Comparator #(.mode("unsigned"), .width(3)) comparator_38 (
    .a(inst[14:12]), .b(3'b000), .eq(comparator_38_eq));  // open: gt, lt
  Comparator #(.mode("unsigned"), .width(7)) comparator_39 (.a(inst[6:0]), .b(7'b0110111), .eq(lui));  // open: gt, lt
  Comparator #(.mode("unsigned"), .width(7)) comparator_40 (.a(inst[6:0]), .b(7'b0010111), .eq(auipc));  // open: gt, lt
  and and_25 (beq, B, comparator_38_eq);
  Comparator #(.mode("unsigned"), .width(32)) comparator_41 (.a(rs1_data), .b(rs2_data), .eq(equal));  // open: gt, lt
  or or_13 (or_13_out, I, I_load, jalr);
  or or_14 (wb_en, R, or_13_out, U, jal);

  assign flush = control_en;
  assign S = mem_wen;

  // Other names for the same wires on the sheet: opcode[6:0] = inst[6:0]; imm_4_0[4:0] = inst[11:7];
  //   imm_11_b = inst[7]; wb_address[4:0] = inst[11:7]; imm_4_1[3:0] = inst[11:8]; func3[2:0] = inst[14:12];
  //   imm_19_12[7:0] = inst[19:12]; imm_31_12[19:0] = inst[31:12]; rs1[4:0] = inst[19:15];
  //   imm_11_0[11:0] = inst[31:20]; imm_11_j = inst[20]; rs2[4:0] = inst[24:20]; imm_10_1[9:0] = inst[30:21];
  //   func7[6:0] = inst[31:25]; imm_10_5[5:0] = inst[30:25]; imm_11_5[6:0] = inst[31:25]; imm_12 = inst[31];
  //   imm_20 = inst[31]

  // Notes on the sheet:
  //   alu_ctrl
  //   control_en and flush
  //   wb_src
  //   op1_src, op2_src
  //   mem_wen
  //   rs1, rs2, compare
  //   wb_en
endmodule
